# Fritzing sketch EHP2 (saved by Fritzing 1.0.5)
breadboards: 1

parts:
  Pico/Pico2_Mod_1 = Raspberry Pi Pico or Pico 2
  S1 = Pushbutton [package="[THT]"]
  S2 = Pushbutton [package="[THT]"]
  S3 = Pushbutton [package="[THT]"]
  S4 = Pushbutton [package="[THT]"]
  S5 = Pushbutton [package="[THT]"]
  LED1 = smd LED [color="Red (633nm)" package="0603 [SMD]"]
  LED2 = smd LED [color="Green (555nm)" package="0603 [SMD]"]
  LED3 = smd LED [color="Blue (430nm)" package="0603 [SMD]"]
  LED4 = smd LED [color="Yellow (595nm)" package="0603 [SMD]"]
  R2 = Resistor [tolerance=±5% power=0.25W resistance=220 package=THT]
  R3 = Resistor [tolerance=±5% power=0.25W resistance=220 package=THT]
  R4 = Resistor [tolerance=±5% power=0.25W resistance=220 package=THT]
  R5 = Resistor [tolerance=±5% power=0.25W resistance=220 package=THT]

nets:
  N1: Pico/Pico2_Mod_1.pin_3, Pico/Pico2_Mod_1.pin_8, Pico/Pico2_Mod_1.pin_13, Pico/Pico2_Mod_1.pin_18, Pico/Pico2_Mod_1.pin_23, Pico/Pico2_Mod_1.pin_28, Pico/Pico2_Mod_1.pin_33, Pico/Pico2_Mod_1.pin_38, Pico/Pico2_Mod_1.pin_42, S1.Pin_1, S1.Pin_2, S2.Pin_1, S2.Pin_2, S3.Pin_1, S3.Pin_2, S4.Pin_1, S4.Pin_2, S5.Pin_1, S5.Pin_2, R2.Pin_1, R4.Pin_1, R5.Pin_1
  N2: Pico/Pico2_Mod_1.pin_9, S5.Pin_3, S5.Pin_4
  N3: Pico/Pico2_Mod_1.pin_10, S4.Pin_3, S4.Pin_4
  N4: Pico/Pico2_Mod_1.pin_11, S3.Pin_3, S3.Pin_4
  N5: Pico/Pico2_Mod_1.pin_12, S2.Pin_3, S2.Pin_4
  N6: Pico/Pico2_Mod_1.pin_21, LED1.anode
  N7: Pico/Pico2_Mod_1.pin_22, LED2.anode
  N8: Pico/Pico2_Mod_1.pin_24, LED3.anode
  N9: Pico/Pico2_Mod_1.pin_25, LED4.anode
  N10: Pico/Pico2_Mod_1.pin_30, S1.Pin_3, S1.Pin_4
  N11: LED1.cathode, R5.Pin_0
  N12: LED2.cathode, R4.Pin_0
  N13: LED3.cathode, R3.Pin_0
  N14: LED4.cathode, R2.Pin_0

custom parts:
  Raspberry Pi Pico or Pico 2: Raspberry Pi Pico and Pico 2. Based around the RP2040 and RP2350 microcontrollers respectively, Picos are low cost microcontroller device bringing Raspberry Pi quality, cost, and easy of use to the microcontroller space. Jan 2021, Split part in to two versions: tht (this one) and SMD. This one will drill holes for a .1 in header in pcb to allow plugging in the module as well as providing pads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
